// Digital circuit cpu.dig as structural Verilog
module cpu (
  input  in_1,
  input  in_2,
  input  in_3,
  input  in_4,
  input  in_5,
  input  in_6,
  input  in_7,
  input  in_8,
  input  in_9,
  input  clk
);

  wire adder_1_p10, adder_1_p11, adder_1_p12, adder_1_p13, and_1_out, and_2_out, and_3_out, and_4_out,
       and_5_out, button_1_out, counter_resetable_1_o_0, counter_resetable_1_o_1, counter_resetable_1_o_2,
       counter_resetable_1_o_3, counter_resetable_2_o_0, counter_resetable_2_o_1, counter_resetable_2_o_2,
       counter_resetable_2_o_3, counter_resetable_3_o_0, counter_resetable_3_o_1, counter_resetable_3_o_2,
       counter_resetable_3_o_3, curr_instr_w, decoder_6_to_64_1_p5, decoder_6_to_64_1_p6,
       decoder_6_to_64_1_p7, decoder_6_to_64_1_p8, decoder_6_to_64_1_p10, decoder_6_to_64_1_p11,
       decoder_6_to_64_1_p12, decoder_6_to_64_1_p13, decoder_6_to_64_1_p14, decoder_6_to_64_1_p15,
       decoder_6_to_64_1_p16, decoder_6_to_64_1_p17, decoder_6_to_64_1_p18, decoder_6_to_64_1_p19,
       decoder_6_to_64_1_p20, decoder_6_to_64_1_p21, halt, jk_async_resetable_flip_flop_1_q,
       jk_async_resetable_flip_flop_1_q_2, load_A, madr_q_0, madr_q_1, madr_q_2, madr_q_3, madr_w, mem_r,
       memory2_1_o_0, memory2_1_o_1, memory2_1_o_2, memory2_1_o_3, memory2_1_o_4, memory2_1_o_5,
       memory2_1_o_6, memory2_1_o_7, not_1_out, not_2_out, not_3_out, not_4_out, not_5_out, or_1_out,
       or_2_out, pc_inc, pc_r, register_simple_1_q_0, register_simple_1_q_1, register_simple_1_q_2,
       register_simple_1_q_3, register_simple_2_q_0, register_simple_2_q_1, register_simple_2_q_2,
       register_simple_2_q_3, reset, rising_edge_detector_2_o, tri_state_buffer_4bit_1_o_0,
       tri_state_buffer_4bit_1_o_1, tri_state_buffer_4bit_1_o_2, tri_state_buffer_4bit_1_o_3,
       tri_state_buffer_4bit_2_o_0, tri_state_buffer_4bit_2_o_1, tri_state_buffer_4bit_2_o_2,
       tri_state_buffer_4bit_2_o_3, xor_1_out;
  wire [7:0] dipswitch_14_out, driver_1_out, driver_2_out, rom_buffer_1_p3;

  rising_edge_detector rising_edge_detector_1 (.CLK(button_1_out), .O(reset));
  Button #(.activeLow("true")) button_1 (.out(button_1_out));
  rising_edge_detector rising_edge_detector_2 (.CLK(and_5_out), .O(rising_edge_detector_2_o));
  or or_1 (or_1_out, halt, clk);
  JK_async_resetable_flip_flop jk_async_resetable_flip_flop_1 (
    .C(rising_edge_detector_2_o), .S(1'b1), .R(1'b1), .R_a(reset), .Q(jk_async_resetable_flip_flop_1_q),
    .Q_2(jk_async_resetable_flip_flop_1_q_2));
  not not_1 (not_1_out, or_1_out);
  and and_1 (and_1_out, or_1_out, jk_async_resetable_flip_flop_1_q_2);
  xor xor_1 (xor_1_out, and_1_out, and_4_out);
  counter_resetable counter_resetable_1 (
    .C(xor_1_out), .R(reset), .S(1'b0), .D_0(1'b0), .D_1(1'b0), .D_2(1'b0), .D_3(1'b0),
    .O_0(counter_resetable_1_o_0), .O_1(counter_resetable_1_o_1), .O_2(counter_resetable_1_o_2),
    .O_3(counter_resetable_1_o_3));  // open: R_a
  not not_2 (not_2_out, counter_resetable_1_o_0);
  not not_3 (not_3_out, counter_resetable_1_o_1);
  not not_4 (not_4_out, counter_resetable_1_o_2);
  not not_5 (not_5_out, counter_resetable_1_o_3);
  and and_2 (and_2_out, not_2_out, not_3_out, not_4_out, not_5_out);
  and and_3 (and_3_out, counter_resetable_1_o_0, not_3_out, not_4_out, not_5_out);
  and and_4 (and_4_out, not_2_out, counter_resetable_1_o_1);
  and and_5 (and_5_out, counter_resetable_1_o_0, counter_resetable_1_o_1);
  DipSwitch #(.dipDefault("true")) dipswitch_1 (.out(rom_buffer_1_p3[0]));
  DipSwitch dipswitch_2 (.out(dipswitch_14_out[0]));
  DipSwitch dipswitch_3 (.out(rom_buffer_1_p3[4]));
  DipSwitch dipswitch_4 (.out(rom_buffer_1_p3[3]));
  DipSwitch dipswitch_5 (.out(rom_buffer_1_p3[2]));
  DipSwitch #(.dipDefault("true")) dipswitch_6 (.out(rom_buffer_1_p3[1]));
  DipSwitch dipswitch_7 (.out(dipswitch_14_out[4]));
  DipSwitch dipswitch_8 (.out(dipswitch_14_out[1]));
  DipSwitch #(.dipDefault("true")) dipswitch_9 (.out(dipswitch_14_out[2]));
  DipSwitch #(.dipDefault("true")) dipswitch_10 (.out(dipswitch_14_out[3]));
  // rom_buffer rom_buffer_1: pin names not known; wires that end beside it: and_2_out, and_2_out, rom_buffer_1_p3, pc_r, madr_w
  DipSwitch dipswitch_11 (.out(rom_buffer_1_p3[7]));
  DipSwitch dipswitch_12 (.out(rom_buffer_1_p3[6]));
  DipSwitch dipswitch_13 (.out(rom_buffer_1_p3[5]));
  rom_buffer rom_buffer_2 (
    .E(and_3_out), .D(dipswitch_14_out), .O_2(mem_r), .O_3(curr_instr_w), .O_6(pc_inc));  // open: O_0, O_1, O_4, O_5, O_7
  DipSwitch dipswitch_14 (.out(dipswitch_14_out[7]));
  DipSwitch #(.dipDefault("true")) dipswitch_15 (.out(dipswitch_14_out[6]));
  DipSwitch dipswitch_16 (.out(dipswitch_14_out[5]));
  or or_2 (or_2_out, and_4_out, and_5_out);
  counter_resetable counter_resetable_2 (
    .C(or_1_out), .R(and_3_out), .S(1'b0), .D_0(1'b0), .D_1(1'b0), .D_2(1'b0), .D_3(1'b0),
    .O_0(counter_resetable_2_o_0), .O_1(counter_resetable_2_o_1), .O_2(counter_resetable_2_o_2),
    .O_3(counter_resetable_2_o_3));  // open: R_a
  // decoder_6_to_64 decoder_6_to_64_1: pin names not known; wires that end beside it: counter_resetable_2_o_2, counter_resetable_2_o_3, counter_resetable_2_o_0, counter_resetable_2_o_1, decoder_6_to_64_1_p5, decoder_6_to_64_1_p6, decoder_6_to_64_1_p7, decoder_6_to_64_1_p8, or_2_out, decoder_6_to_64_1_p10, decoder_6_to_64_1_p11, decoder_6_to_64_1_p12, decoder_6_to_64_1_p13, decoder_6_to_64_1_p14, decoder_6_to_64_1_p15, decoder_6_to_64_1_p16, decoder_6_to_64_1_p17, decoder_6_to_64_1_p18, decoder_6_to_64_1_p19, decoder_6_to_64_1_p20, decoder_6_to_64_1_p21, decoder_6_to_64_1_p14, decoder_6_to_64_1_p15, decoder_6_to_64_1_p16, decoder_6_to_64_1_p18, decoder_6_to_64_1_p19, decoder_6_to_64_1_p20
  assign {driver_1_out[7:5], halt, driver_1_out[3:0]} = decoder_6_to_64_1_p13 ? 8'h10 : 8'bz;  // Driver driver_1
  assign {driver_2_out[7:6], load_A, driver_2_out[4:3], mem_r, driver_2_out[1:0]} = decoder_6_to_64_1_p17 ? 8'h24 : 8'bz;  // Driver driver_2
  register_simple madr (
    .E_out(madr_w), .CLK(not_1_out), .D_0(tri_state_buffer_4bit_1_o_0), .D_1(tri_state_buffer_4bit_1_o_1),
    .D_2(tri_state_buffer_4bit_1_o_2), .D_3(tri_state_buffer_4bit_1_o_3), .Q_0(madr_q_0), .Q_1(madr_q_1),
    .Q_2(madr_q_2), .Q_3(madr_q_3));
  PullDown pulldown_1 (.out(pc_inc));
  memory2 memory2_1 (
    .a_0(madr_q_0), .a_1(madr_q_1), .a_2(madr_q_2), .a_3(madr_q_3), .E(in_2), .C(not_1_out),
    .D_0(tri_state_buffer_4bit_1_o_0), .D_1(tri_state_buffer_4bit_1_o_1), .D_2(tri_state_buffer_4bit_1_o_2),
    .D_3(tri_state_buffer_4bit_1_o_3), .O_0(memory2_1_o_0), .O_1(memory2_1_o_1), .O_2(memory2_1_o_2),
    .O_3(memory2_1_o_3), .O_4(memory2_1_o_4), .O_5(memory2_1_o_5), .O_6(memory2_1_o_6), .O_7(memory2_1_o_7));
  PullDown pulldown_2 (.out(halt));
  PullDown pulldown_3 (.out(load_A));
  PullDown pulldown_4 (.out(mem_r));
  PullDown pulldown_5 (.out(curr_instr_w));
  PullDown pulldown_6 (.out(madr_w));
  PullDown pulldown_7 (.out(pc_r));
  tri_state_buffer_4bit tri_state_buffer_4bit_1 (
    .D_0(memory2_1_o_0), .D_1(memory2_1_o_1), .D_2(memory2_1_o_2), .D_3(memory2_1_o_3), .E(mem_r),
    .O_0(tri_state_buffer_4bit_1_o_0), .O_1(tri_state_buffer_4bit_1_o_1), .O_2(tri_state_buffer_4bit_1_o_2),
    .O_3(tri_state_buffer_4bit_1_o_3));
  tri_state_buffer_4bit tri_state_buffer_4bit_2 (
    .D_0(memory2_1_o_4), .D_1(memory2_1_o_5), .D_2(memory2_1_o_6), .D_3(memory2_1_o_7), .E(mem_r),
    .O_0(tri_state_buffer_4bit_2_o_0), .O_1(tri_state_buffer_4bit_2_o_1), .O_2(tri_state_buffer_4bit_2_o_2),
    .O_3(tri_state_buffer_4bit_2_o_3));
  register_simple Current_Instruction_HI (
    .E_out(curr_instr_w), .CLK(not_1_out), .D_0(tri_state_buffer_4bit_2_o_0),
    .D_1(tri_state_buffer_4bit_2_o_1), .D_2(tri_state_buffer_4bit_2_o_2), .D_3(tri_state_buffer_4bit_2_o_3),
    .Q_0(decoder_6_to_64_1_p5), .Q_1(decoder_6_to_64_1_p6), .Q_2(decoder_6_to_64_1_p7),
    .Q_3(decoder_6_to_64_1_p8));
  register_simple Current_Instruction_LO (
    .E_out(curr_instr_w), .CLK(not_1_out), .D_0(tri_state_buffer_4bit_1_o_0),
    .D_1(tri_state_buffer_4bit_1_o_1), .D_2(tri_state_buffer_4bit_1_o_2), .D_3(tri_state_buffer_4bit_1_o_3),
    .Q_0(decoder_6_to_64_1_p21), .Q_1(decoder_6_to_64_1_p12), .Q_2(decoder_6_to_64_1_p11),
    .Q_3(decoder_6_to_64_1_p10));
  counter_resetable counter_resetable_3 (
    .C(pc_inc), .R(reset), .S(1'b0), .D_0(1'b0), .D_1(1'b0), .D_2(1'b0), .D_3(1'b0),
    .O_0(counter_resetable_3_o_0), .O_1(counter_resetable_3_o_1), .O_2(counter_resetable_3_o_2),
    .O_3(counter_resetable_3_o_3));  // open: R_a
  tri_state_buffer_4bit tri_state_buffer_4bit_3 (
    .D_0(counter_resetable_3_o_0), .D_1(counter_resetable_3_o_1), .D_2(counter_resetable_3_o_2),
    .D_3(counter_resetable_3_o_3), .E(pc_r), .O_0(tri_state_buffer_4bit_1_o_0),
    .O_1(tri_state_buffer_4bit_1_o_1), .O_2(tri_state_buffer_4bit_1_o_2), .O_3(tri_state_buffer_4bit_1_o_3));
  register_simple register_simple_1 (
    .E_out(load_A), .CLK(not_1_out), .D_0(tri_state_buffer_4bit_1_o_0), .D_1(tri_state_buffer_4bit_1_o_1),
    .D_2(tri_state_buffer_4bit_1_o_2), .D_3(tri_state_buffer_4bit_1_o_3), .Q_0(register_simple_1_q_0),
    .Q_1(register_simple_1_q_1), .Q_2(register_simple_1_q_2), .Q_3(register_simple_1_q_3));
  register_simple register_simple_2 (
    .E_out(in_6), .CLK(not_1_out), .D_0(tri_state_buffer_4bit_1_o_0), .D_1(tri_state_buffer_4bit_1_o_1),
    .D_2(tri_state_buffer_4bit_1_o_2), .D_3(tri_state_buffer_4bit_1_o_3), .Q_0(register_simple_2_q_0),
    .Q_1(register_simple_2_q_1), .Q_2(register_simple_2_q_2), .Q_3(register_simple_2_q_3));
  tri_state_buffer_4bit tri_state_buffer_4bit_4 (
    .D_0(adder_1_p10), .D_1(adder_1_p11), .D_2(adder_1_p12), .D_3(adder_1_p13), .E(in_8),
    .O_0(tri_state_buffer_4bit_1_o_0), .O_1(tri_state_buffer_4bit_1_o_1), .O_2(tri_state_buffer_4bit_1_o_2),
    .O_3(tri_state_buffer_4bit_1_o_3));
  tri_state_buffer_4bit tri_state_buffer_4bit_5 (
    .D_0(register_simple_1_q_0), .D_1(register_simple_1_q_1), .D_2(register_simple_1_q_2),
    .D_3(register_simple_1_q_3), .E(in_4), .O_0(tri_state_buffer_4bit_1_o_0),
    .O_1(tri_state_buffer_4bit_1_o_1), .O_2(tri_state_buffer_4bit_1_o_2), .O_3(tri_state_buffer_4bit_1_o_3));
  tri_state_buffer_4bit tri_state_buffer_4bit_6 (
    .D_0(register_simple_2_q_0), .D_1(register_simple_2_q_1), .D_2(register_simple_2_q_2),
    .D_3(register_simple_2_q_3), .E(in_5), .O_0(tri_state_buffer_4bit_1_o_0),
    .O_1(tri_state_buffer_4bit_1_o_1), .O_2(tri_state_buffer_4bit_1_o_2), .O_3(tri_state_buffer_4bit_1_o_3));
  // adder adder_1: pin names not known; wires that end beside it: in_7, register_simple_1_q_0, register_simple_1_q_1, register_simple_1_q_2, register_simple_1_q_3, register_simple_2_q_0, register_simple_2_q_1, register_simple_2_q_2, register_simple_2_q_3, adder_1_p10, adder_1_p11, adder_1_p12, adder_1_p13
endmodule
