// Digital circuit notepad.dig as structural Verilog
module notepad (
  input  D,
  input  CLK,
  output Q,
  output Q_2
);

  wire d_flip_flop_1_q, not_1_out, not_2_out;

  not not_1 (not_1_out, CLK);
  D_flip_flop d_flip_flop_1 (.D(D), .CLK(not_1_out), .Q(d_flip_flop_1_q));  // open: Q_2
  not not_2 (not_2_out, not_1_out);
  D_flip_flop d_flip_flop_2 (.D(d_flip_flop_1_q), .CLK(not_2_out), .Q(Q), .Q_2(Q_2));

  // Notes on the sheet:
  //   generate test headers
  //   tryhaskell.org
  //   concat $ map (\x -> " D_" ++ show x) [63,62..0]
  //   rising edge D flip-flop without delay
endmodule
